# Fritzing sketch circuit-ili9341-ili9488-touch (saved by Fritzing 1.0.4)
breadboards: 1

parts:
  Mod1 = Raspberry Pi Pico
  ILI9341 = Header 8 [package=1x08_smd]
  JP1 = Header 6 [package=1x06_smd_straight_alt]
  ILI9488 = Header 8 [package=1x08_smd]
  JP2 = Header 6 [package=1x06_smd_straight_alt]

nets:
  N1: Mod1.pin_3, Mod1.pin_8, Mod1.pin_13, Mod1.pin_18, Mod1.pin_23, Mod1.pin_28, Mod1.pin_33, Mod1.pin_38, ILI9341.7, ILI9488.7
  N2: Mod1.pin_4, JP1.5, JP2.5
  N3: Mod1.pin_5, JP1.3, JP2.3
  N4: Mod1.pin_6, JP1.2, JP2.2
  N5: Mod1.pin_11, JP1.4
  N6: Mod1.pin_12, JP1.1
  N7: Mod1.pin_14, ILI9341.5
  N8: Mod1.pin_15, ILI9341.4
  N9: Mod1.pin_16, ILI9341.6
  N10: Mod1.pin_17, ILI9341.1
  N11: Mod1.pin_19, ILI9341.2, ILI9488.2
  N12: Mod1.pin_20, ILI9341.3, ILI9488.3
  N13: Mod1.pin_21, JP2.4
  N14: Mod1.pin_22, JP2.1
  N15: Mod1.pin_24, ILI9488.5
  N16: Mod1.pin_25, ILI9488.4
  N17: Mod1.pin_26, ILI9488.6
  N18: Mod1.pin_27, ILI9488.1
  N19: Mod1.pin_36, ILI9341.8, ILI9488.8

notes:
  GND
  VCC
  SCK
  SDI (MOSI)
  DC
  RESET
  CS
  LED
  SDO (MISO)
  T_CS
  T_CLK
  T_DIN (MOSI)
  T_DO (MISO)
  T_IRQ

custom parts:
  Raspberry Pi Pico: Raspberry Pi Pico. Based around the RP2040 microcontroller the Pico is a low cost microcontroller device bringing Raspberry Pi quality, cost, and easy of use to the microcontroller space. Jan 2021, Split part in to two versions: tht (this one) and SMD. This one will drill holes for a .1 in header in pcb to allow plugging in the module as well as providing pads to solder the module to the top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
