# Fritzing sketch circuit-ssd1306-Terminal (saved by Fritzing 1.0.4)
breadboards: 1

parts:
  Mod1 = Raspberry Pi Pico
  S1 = Momentary Switch [package=ksa_sealed_tac_switch]
  S2 = Momentary Switch [package=ksa_sealed_tac_switch]
  S3 = Momentary Switch [package=ksa_sealed_tac_switch]
  S4 = Momentary Switch [package=ksa_sealed_tac_switch]
  SSD1306 = Header 4 [package=jst-4-pth]

nets:
  N1: Mod1.pin_3, Mod1.pin_8, Mod1.pin_13, Mod1.pin_18, Mod1.pin_23, Mod1.pin_28, Mod1.pin_33, Mod1.pin_38, Mod1.pin_42, S1.1, S1.2, S2.1, S2.2, S3.1, S3.2, S4.1, S4.2, SSD1306.4
  N2: Mod1.pin_6, SSD1306.1
  N3: Mod1.pin_7, SSD1306.2
  N4: Mod1.pin_24, S2.3, S2.4
  N5: Mod1.pin_25, S4.3, S4.4
  N6: Mod1.pin_26, S1.3, S1.4
  N7: Mod1.pin_27, S3.3, S3.4
  N8: Mod1.pin_36, SSD1306.3

notes:
  GND
  VCC
  SDA
  SCL
  Roll Up
  Dump
  Roll Down
  Print Buffer

custom parts:
  Raspberry Pi Pico: Raspberry Pi Pico. Based around the RP2040 microcontroller the Pico is a low cost microcontroller device bringing Raspberry Pi quality, cost, and easy of use to the microcontroller space. Jan 2021, Split part in to two versions: tht (this one) and SMD. This one will drill holes for a .1 in header in pcb to allow plugging in the module as well as providing pads to solder the module to the top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
