# Fritzing sketch circuit-keymatrix-st7789 (saved by Fritzing 1.0.4)
breadboards: 1

parts:
  Mod1 = Raspberry Pi Pico
  ST7789 = Header 8 [package=1x08_smd]

nets:
  N1: Mod1.pin_3, Mod1.pin_8, Mod1.pin_13, Mod1.pin_18, Mod1.pin_23, Mod1.pin_28, Mod1.pin_33, Mod1.pin_38, ST7789.1
  N2: Mod1.pin_14, ST7789.5
  N3: Mod1.pin_15, ST7789.6
  N4: Mod1.pin_16, ST7789.7
  N5: Mod1.pin_17, ST7789.8
  N6: Mod1.pin_19, ST7789.3
  N7: Mod1.pin_20, ST7789.4
  N8: Mod1.pin_36, ST7789.2

notes:
  GND
  VCC
  SCL
  SDA
  DC
  RST
  CS
  BL
  VCC (5V)
  row0
  row3
  col0
  col3
  keyboard matrix
  row1
  row2
  col1
  col2

custom parts:
  Raspberry Pi Pico: Raspberry Pi Pico. Based around the RP2040 microcontroller the Pico is a low cost microcontroller device bringing Raspberry Pi quality, cost, and easy of use to the microcontroller space. Jan 2021, Split part in to two versions: tht (this one) and SMD. This one will drill holes for a .1 in header in pcb to allow plugging in the module as well as providing pads to solder the module to the top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
