# Fritzing sketch circuit-st7789 (saved by Fritzing 1.0.4)
breadboards: 1

parts:
  Mod1 = Raspberry Pi Pico
  ST7789 = Header 8 [package=1x08_smd]
  J1 = Piezo Speaker
  R1 = Resistor [tolerance=±5% resistance=100 package="2010 [SMD]"]

nets:
  N1: Mod1.pin_3, Mod1.pin_8, Mod1.pin_13, Mod1.pin_18, Mod1.pin_23, Mod1.pin_28, Mod1.pin_33, Mod1.pin_38, Mod1.pin_42, ST7789.1, J1.pin1
  N2: Mod1.pin_10, R1.Pin_1
  N3: Mod1.pin_15, ST7789.7
  N4: Mod1.pin_16, ST7789.6
  N5: Mod1.pin_17, ST7789.5
  N6: Mod1.pin_24, ST7789.3
  N7: Mod1.pin_25, ST7789.4
  N8: Mod1.pin_36, ST7789.2, ST7789.8
  N9: J1.pin2, R1.Pin_0

notes:
  GND
  VCC
  SCL
  SDA
  DC
  RST
  CS
  BL
  100 Ω

custom parts:
  Raspberry Pi Pico: Raspberry Pi Pico. Based around the RP2040 microcontroller the Pico is a low cost microcontroller device bringing Raspberry Pi quality, cost, and easy of use to the microcontroller space. Jan 2021, Split part in to two versions: tht (this one) and SMD. This one will drill holes for a .1 in header in pcb to allow plugging in the module as well as providing pads to solder the module to the top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
