# Fritzing sketch circuit-st7789-multi (saved by Fritzing 1.0.4)
breadboards: 1

parts:
  Mod1 = Raspberry Pi Pico
  ST7789 = Header 8 [package=1x08_smd]
  ST7789_2 = Header 8 [package=1x08_smd]

nets:
  N1: Mod1.pin_3, Mod1.pin_8, Mod1.pin_13, Mod1.pin_18, Mod1.pin_23, Mod1.pin_28, Mod1.pin_33, Mod1.pin_38, ST7789.1, ST7789_2.1
  N2: Mod1.pin_14, ST7789.5
  N3: Mod1.pin_15, ST7789.6
  N4: Mod1.pin_16, ST7789.7
  N5: Mod1.pin_17, ST7789.8
  N6: Mod1.pin_19, ST7789.3, ST7789_2.3
  N7: Mod1.pin_20, ST7789.4, ST7789_2.4
  N8: Mod1.pin_24, ST7789_2.5
  N9: Mod1.pin_25, ST7789_2.6
  N10: Mod1.pin_26, ST7789_2.7
  N11: Mod1.pin_27, ST7789_2.8
  N12: Mod1.pin_36, ST7789.2, ST7789_2.2

notes:
  GND
  VCC
  SCL
  SDA
  DC
  RST
  CS
  BL

custom parts:
  Raspberry Pi Pico: Raspberry Pi Pico. Based around the RP2040 microcontroller the Pico is a low cost microcontroller device bringing Raspberry Pi quality, cost, and easy of use to the microcontroller space. Jan 2021, Split part in to two versions: tht (this one) and SMD. This one will drill holes for a .1 in header in pcb to allow plugging in the module as well as providing pads to solder the module to the top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
