# Fritzing sketch circuit-usbhost (saved by Fritzing 1.0.4)
breadboards: 1

parts:
  Mod1 = Raspberry Pi Pico
  R1 = Resistor [tolerance=±5% resistance=220 package="2010 [SMD]"]
  R2 = Resistor [tolerance=±5% resistance=220 package="2010 [SMD]"]
  R3 = Resistor [tolerance=±5% resistance=220 package="2010 [SMD]"]
  R4 = Resistor [tolerance=±5% resistance=220 package="2010 [SMD]"]
  LED7 = LED - 5mm [color="Blue (470nm)" current=0.030A package="5 mm [THT]"]
  LED8 = LED - 5mm [color="Yellow (585nm)" current=0.030A package="5 mm [THT]"]
  LED9 = LED - 5mm [color="Red (633nm)" current=0.030A package="5 mm [THT]"]
  LED10 = LED - 5mm [color="Green (560nm)" current=0.030A package="5 mm [THT]"]

nets:
  N1: Mod1.pin_3, Mod1.pin_8, Mod1.pin_13, Mod1.pin_18, Mod1.pin_23, Mod1.pin_28, Mod1.pin_33, Mod1.pin_38, Mod1.pin_42, LED7.cathode, LED8.cathode, LED9.cathode, LED10.cathode
  N2: Mod1.pin_24, R1.Pin_0
  N3: Mod1.pin_25, R2.Pin_0
  N4: Mod1.pin_26, R3.Pin_0
  N5: Mod1.pin_27, R4.Pin_0
  N6: R1.Pin_1, LED10.anode
  N7: R2.Pin_1, LED9.anode
  N8: R3.Pin_1, LED8.anode
  N9: R4.Pin_1, LED7.anode

notes:
  VCC (5V)
  GND
  220 Ω x 4

custom parts:
  Raspberry Pi Pico: Raspberry Pi Pico. Based around the RP2040 microcontroller the Pico is a low cost microcontroller device bringing Raspberry Pi quality, cost, and easy of use to the microcontroller space. Jan 2021, Split part in to two versions: tht (this one) and SMD. This one will drill holes for a .1 in header in pcb to allow plugging in the module as well as providing pads to solder the module to the top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
